# Fritzing sketch wee (saved by Fritzing 0.9.3b)
breadboards: 1

parts:
  Componente1 = Arduino Uno (Rev3)
  S1 = H-Bridge with L298N
  HC-SR04_Sensor_1 = HC-SR04 Ultrasonic Distance Sensor
  J1 = Basic Servo
  M1 = DC Motor
  M2 = DC Motor
  BAT1 = BC9VPC [package=bc9vpc]

nets:
  N1: Componente1.D8, S1.IN3
  N2: Componente1.D9_PWM, S1.IN4
  N3: Componente1.D10_PWM/SS, S1.ENA
  N4: Componente1.D11_PWM/MOSI, S1.ENB
  N5: Componente1.D2, HC-SR04_Sensor_1.TRIG
  N6: Componente1.D3_PWM, HC-SR04_Sensor_1.ECHO
  N7: Componente1.D5_PWM, J1.pulse
  N8: Componente1.D6_PWM, S1.IN1
  N9: Componente1.D7, S1.IN2
  VCC: Componente1.5V, HC-SR04_Sensor_1.VCC, J1.vcc
  GND: Componente1.GND, HC-SR04_Sensor_1.GND, J1.gnd
  N10: S1.12V, BAT1.V+
  N11: S1.GND, BAT1.V-
  N12: S1.M1-01, M1.pin_1
  N13: S1.M1-02, M1.pin_2
  N14: S1.M2-01, M2.pin_2
  N15: S1.M2-02, M2.pin_1

custom parts:
  H-Bridge with L298N: h-bridge
